// Logisim project protipschetchika1.circ as structural Verilog: 5 circuits, main circuit main
module main (
);

  wire and_1_out, and_2_out, clock_1_out, j_k_ff_1_qn, j_k_ff_2_qn, j_k_ff_3_qn, nand_1_out, xnor_1_out,
       xnor_2_out, xnor_3_out, xnor_4_out;
  wire [3:0] j_k_ff_1_q;

  Clock clock_1 (.out(clock_1_out));
  Hex_Digit_Display hex_digit_display_1 (.value(j_k_ff_1_q));  // open: dp
  and and_1 (and_1_out, 1'b1, nand_1_out);
  J_K_Flip_Flop j_k_ff_1 (
    .J(and_1_out), .K(1'b1), .clk(clock_1_out), .Q(j_k_ff_1_q[0]), .Qn(j_k_ff_1_qn));  // open: preset, reset
  J_K_Flip_Flop j_k_ff_2 (
    .J(and_1_out), .K(1'b1), .clk(j_k_ff_1_qn), .Q(j_k_ff_1_q[1]), .Qn(j_k_ff_2_qn));  // open: preset, reset
  xnor xnor_1 (xnor_1_out, j_k_ff_1_q[0], 1'b1);
  J_K_Flip_Flop j_k_ff_3 (
    .J(and_1_out), .K(1'b1), .clk(j_k_ff_2_qn), .Q(j_k_ff_1_q[2]), .Qn(j_k_ff_3_qn));  // open: preset, reset
  xnor xnor_2 (xnor_2_out, j_k_ff_1_q[1], 1'b0);
  nand nand_1 (nand_1_out, xnor_1_out, xnor_2_out, xnor_3_out, xnor_4_out);
  and and_2 (and_2_out, j_k_ff_3_qn, nand_1_out);
  xnor xnor_3 (xnor_3_out, j_k_ff_1_q[2], 1'b0);
  J_K_Flip_Flop j_k_ff_4 (.J(and_1_out), .K(1'b1), .clk(and_2_out), .Q(j_k_ff_1_q[3]));  // open: Qn, preset, reset
  xnor xnor_4 (xnor_4_out, j_k_ff_1_q[3], 1'b1);
endmodule

module JKTrigger (
  input  in_1,
  input  in_2,
  input  in_3,
  input  in_4,
  output out_5,
  output out_6
);

  wire nand_1_out, nand_2_out;

  nand nand_1 (nand_1_out, in_1, in_2, out_6);
  nand nand_2 (nand_2_out, out_5, in_2, in_3);
  nand nand_3 (out_5, nand_1_out, out_6);
  nand nand_4 (out_6, out_5, nand_2_out);
endmodule

module JK2 (
  input  K,
  input  C,
  input  J,
  input  zero,
  input  reset,
  output Q1,
  output Q2
);

  wire and_1_out, and_2_out, not_1_out, rs_2_out_6, rs_2_out_7;

  and and_1 (and_1_out, rs_2_out_6, K);
  and and_2 (and_2_out, J, rs_2_out_7);
  // RS rs_1: pin names not known; wires that end beside it: reset, and_1_out, C, and_2_out, zero, Q1, Q2
  not not_1 (not_1_out, C);
  RS rs_2 (.in_1(Q2), .in_2(not_1_out), .in_3(Q1), .reset(zero), .out_6(rs_2_out_6), .out_7(rs_2_out_7));  // open: zero
endmodule

module RS (
  input  in_1,
  input  in_2,
  input  in_3,
  input  zero,
  input  reset,
  output out_6,
  output out_7
);

  wire and_1_out, and_2_out;

  and and_1 (and_1_out, in_1, in_2);
  and and_2 (and_2_out, in_2, in_3);
  nor nor_1 (out_6, and_1_out, zero, out_7);
  nor nor_2 (out_7, out_6, reset, and_2_out);
endmodule

module Mycounter (
  input  in_1
);

  wire and_1_out, button_1_out, jk2_1_p1, jk2_1_p7, jk2_2_q2, jk2_3_q2, not_1_out;
  wire [3:0] jk2_1_p6;

  Button button_1 (.out(button_1_out));
  Hex_Digit_Display hex_digit_display_1 (.value(jk2_1_p6));  // open: dp
  // JK2 jk2_1: pin names not known; wires that end beside it: jk2_1_p1, 1'b1, in_1, 1'b1, button_1_out, jk2_1_p6[0], jk2_1_p7
  JK2 jk2_2 (.K(1'b1), .C(jk2_1_p7), .J(1'b1), .zero(button_1_out), .Q1(jk2_1_p6[1]), .Q2(jk2_2_q2));  // open: reset
  JK2 jk2_3 (.K(1'b1), .C(jk2_2_q2), .J(1'b1), .zero(button_1_out), .Q1(jk2_1_p6[2]), .Q2(jk2_3_q2));  // open: reset
  and and_1 (and_1_out, jk2_1_p6[0], jk2_2_q2, jk2_3_q2, jk2_1_p6[3]);
  not not_1 (not_1_out, in_1);
  JK2 jk2_4 (.K(1'b1), .C(jk2_3_q2), .J(1'b1), .zero(button_1_out), .Q1(jk2_1_p6[3]));  // open: reset, Q2
  RS rs_1 (
    .in_1(in_1), .in_2(not_1_out), .in_3(and_1_out), .zero(button_1_out), .out_6(jk2_1_p1));  // open: reset, out_7
endmodule
