// Logisim project sqrt.circ as structural Verilog
module FullAdder (
  input  X,
  input  Y,
  input  C0,
  output Z,
  output C1
);

  wire and_1_out, and_2_out, xor_1_out;

  and and_1 (and_1_out, X, Y);
  xor xor_1 (xor_1_out, X, Y);
  and and_2 (and_2_out, xor_1_out, C0);
  xor xor_2 (Z, xor_1_out, C0);
  or or_1 (C1, and_1_out, and_2_out);
endmodule

module DeductorAndComparator (
  input  x0,
  input  y0,
  input  x1,
  input  y1,
  input  x2,
  input  y2,
  input  x3,
  input  y3,
  input  x4,
  input  y4,
  input  x5,
  input  y5,
  input  x6,
  input  y6,
  input  x7,
  input  y7,
  output v0,
  output v1,
  output v2,
  output v3,
  output v4,
  output v5,
  output v6,
  output v7,
  output v8
);

  wire fulladder_1_c1, fulladder_1_z, fulladder_2_c1, fulladder_2_z, fulladder_3_c1, fulladder_3_z,
       fulladder_4_c1, fulladder_4_z, fulladder_5_c1, fulladder_5_z, fulladder_6_c1, fulladder_6_z,
       fulladder_7_c1, fulladder_7_z, fulladder_8_z, not_1_out, not_2_out, not_3_out, not_4_out, not_5_out,
       not_6_out, not_7_out, not_8_out;

  not not_1 (not_1_out, y0);
  FullAdder fulladder_1 (.C1(fulladder_1_c1), .Z(fulladder_1_z), .C0(1'b1), .X(x0), .Y(not_1_out));
  not not_2 (not_2_out, y1);
  FullAdder fulladder_2 (.C1(fulladder_2_c1), .Z(fulladder_2_z), .C0(fulladder_1_c1), .X(x1), .Y(not_2_out));
  not not_3 (not_3_out, y2);
  FullAdder fulladder_3 (.C1(fulladder_3_c1), .Z(fulladder_3_z), .C0(fulladder_2_c1), .X(x2), .Y(not_3_out));
  not not_4 (not_4_out, y3);
  FullAdder fulladder_4 (.C1(fulladder_4_c1), .Z(fulladder_4_z), .C0(fulladder_3_c1), .X(x3), .Y(not_4_out));
  not not_5 (not_5_out, y4);
  FullAdder fulladder_5 (.C1(fulladder_5_c1), .Z(fulladder_5_z), .C0(fulladder_4_c1), .X(x4), .Y(not_5_out));
  not not_6 (not_6_out, y5);
  FullAdder fulladder_6 (.C1(fulladder_6_c1), .Z(fulladder_6_z), .C0(fulladder_5_c1), .X(x5), .Y(not_6_out));
  not not_7 (not_7_out, y6);
  FullAdder fulladder_7 (.C1(fulladder_7_c1), .Z(fulladder_7_z), .C0(fulladder_6_c1), .X(x6), .Y(not_7_out));
  not not_8 (not_8_out, y7);
  FullAdder fulladder_8 (.C1(v8), .Z(fulladder_8_z), .C0(fulladder_7_c1), .X(x7), .Y(not_8_out));
  minicomparator minicomparator_1 (.out_4(v0), .newBit(fulladder_1_z), .highBit(v8), .lastBit(x0));
  minicomparator minicomparator_2 (.out_4(v1), .newBit(fulladder_2_z), .highBit(v8), .lastBit(x1));
  minicomparator minicomparator_3 (.out_4(v2), .newBit(fulladder_3_z), .highBit(v8), .lastBit(x2));
  minicomparator minicomparator_4 (.out_4(v3), .newBit(fulladder_4_z), .highBit(v8), .lastBit(x3));
  minicomparator minicomparator_5 (.out_4(v4), .newBit(fulladder_5_z), .highBit(v8), .lastBit(x4));
  minicomparator minicomparator_6 (.out_4(v5), .newBit(fulladder_6_z), .highBit(v8), .lastBit(x5));
  minicomparator minicomparator_7 (.out_4(v6), .newBit(fulladder_7_z), .highBit(v8), .lastBit(x6));
  minicomparator minicomparator_8 (.out_4(v7), .newBit(fulladder_8_z), .highBit(v8), .lastBit(x7));
endmodule

module SQRT (
  input  x7,
  input  x6,
  input  x5,
  input  x4,
  input  x3,
  input  x2,
  input  x1,
  input  x0,
  output a3,
  output a2,
  output a1,
  output a0
);

  wire deductorandcomparator_1_v0, deductorandcomparator_1_v1, deductorandcomparator_2_v0,
       deductorandcomparator_2_v1, deductorandcomparator_2_v2, deductorandcomparator_2_v3,
       deductorandcomparator_2_v4, deductorandcomparator_2_v5, deductorandcomparator_4_v0,
       deductorandcomparator_4_v1, deductorandcomparator_4_v2, deductorandcomparator_4_v3;

  DeductorAndComparator deductorandcomparator_1 (
    .x0(x6), .y0(1'b1), .x1(x7), .v0(deductorandcomparator_1_v0), .v1(deductorandcomparator_1_v1), .v8(a3));  // open: y1, x2, y2, x3, y3, x4, y4, x5, y5, x6, y6, x7, y7, v2, v3, v4, v5, v6, v7
  DeductorAndComparator deductorandcomparator_2 (
    .x0(x2), .y0(1'b1), .x1(x3), .x2(deductorandcomparator_4_v0), .y2(a2), .x3(deductorandcomparator_4_v1),
    .y3(a3), .x4(deductorandcomparator_4_v2), .x5(deductorandcomparator_4_v3),
    .v0(deductorandcomparator_2_v0), .v1(deductorandcomparator_2_v1), .v2(deductorandcomparator_2_v2),
    .v3(deductorandcomparator_2_v3), .v4(deductorandcomparator_2_v4), .v5(deductorandcomparator_2_v5), .v8(a1));  // open: y1, y4, y5, x6, y6, x7, y7, v6, v7
  DeductorAndComparator deductorandcomparator_3 (
    .x0(x0), .y0(1'b1), .x1(x1), .x2(deductorandcomparator_2_v0), .y2(a1), .x3(deductorandcomparator_2_v1),
    .y3(a2), .x4(deductorandcomparator_2_v2), .y4(a3), .x5(deductorandcomparator_2_v3),
    .x6(deductorandcomparator_2_v4), .x7(deductorandcomparator_2_v5), .v8(a0));  // open: y1, y5, y6, y7, v0, v1, v2, v3, v4, v5, v6, v7
  DeductorAndComparator deductorandcomparator_4 (
    .x0(x4), .y0(1'b1), .x1(x5), .x2(deductorandcomparator_1_v0), .y2(a3), .x3(deductorandcomparator_1_v1),
    .v0(deductorandcomparator_4_v0), .v1(deductorandcomparator_4_v1), .v2(deductorandcomparator_4_v2),
    .v3(deductorandcomparator_4_v3), .v8(a2));  // open: y1, y3, x4, y4, x5, y5, x6, y6, x7, y7, v4, v5, v6, v7
endmodule

module minicomparator (
  input  lastBit,
  input  newBit,
  input  highBit,
  output out_4
);

  wire and_1_out, and_2_out, not_1_out;

  not not_1 (not_1_out, highBit);
  and and_1 (and_1_out, newBit, highBit);
  and and_2 (and_2_out, lastBit, not_1_out);
  or or_1 (out_4, and_2_out, and_1_out);
endmodule
