// Logisim project Schemes EVM1 (1).circ as structural Verilog
module \СКНФ  (
);

  wire and_1_out, and_2_out, and_3_out, and_4_out, and_5_out, and_6_out, and_7_out, not_1_out, not_2_out,
       not_3_out, not_4_out, not_5_out, not_6_out, not_7_out, not_8_out, or_1_out, or_2_out, or_3_out,
       or_4_out, or_5_out, or_6_out, or_7_out, or_8_out, or_9_out, or_10_out, or_11_out, or_12_out,
       or_13_out, or_14_out, or_15_out, or_16_out, X0_out, X1_out, X2_out, X3_out;

  Clock #(.highDuration(8), .lowDuration(8)) X3 (.out(X3_out));
  Clock #(.highDuration(4), .lowDuration(4)) X2 (.out(X2_out));
  Clock #(.highDuration(2), .lowDuration(2)) X1 (.out(X1_out));
  Clock X0 (.out(X0_out));
  not not_1 (not_1_out, X2_out);
  not not_2 (not_2_out, X3_out);
  not not_3 (not_3_out, X2_out);
  not not_4 (not_4_out, X3_out);
  not not_5 (not_5_out, X0_out);
  not not_6 (not_6_out, X1_out);
  not not_7 (not_7_out, X0_out);
  not not_8 (not_8_out, X1_out);
  or or_1 (or_1_out, X3_out, X2_out);
  or or_2 (or_2_out, X3_out, not_1_out);
  or or_3 (or_3_out, not_2_out, X2_out);
  or or_4 (or_4_out, not_3_out, not_4_out);
  or or_5 (or_5_out, not_5_out, not_6_out);
  or or_6 (or_6_out, X1_out, not_7_out);
  or or_7 (or_7_out, not_8_out, X0_out);
  or or_8 (or_8_out, X0_out, X1_out);
  or or_9 (or_9_out, or_4_out, or_5_out);
  or or_10 (or_10_out, or_2_out, or_5_out);
  or or_11 (or_11_out, or_1_out, or_5_out);
  or or_12 (or_12_out, or_4_out, or_6_out);
  or or_13 (or_13_out, or_2_out, or_7_out);
  or or_14 (or_14_out, or_3_out, or_7_out);
  or or_15 (or_15_out, or_2_out, or_8_out);
  or or_16 (or_16_out, or_3_out, or_8_out);
  and and_1 (and_1_out, or_9_out, or_10_out);
  and and_2 (and_2_out, and_1_out, and_3_out);
  and and_3 (and_3_out, or_11_out, or_12_out);
  and and_4 (and_4_out, or_13_out, or_14_out);
  and and_5 (and_5_out, and_4_out, and_6_out);
  and and_6 (and_6_out, or_15_out, or_16_out);
  and and_7 (and_7_out, and_2_out, and_5_out);
  LED led_1 (.in(and_7_out));
endmodule

module \МДНФ  (
);

  wire and_1_out, and_2_out, and_3_out, and_4_out, and_5_out, and_6_out, and_7_out, and_8_out, not_1_out,
       not_2_out, not_3_out, not_4_out, or_1_out, or_2_out, or_3_out, X0_out, X1_out, X2_out, X3_out;

  Clock #(.highDuration(8), .lowDuration(8)) X3 (.out(X3_out));
  Clock #(.highDuration(4), .lowDuration(4)) X2 (.out(X2_out));
  Clock #(.highDuration(2), .lowDuration(2)) X1 (.out(X1_out));
  Clock X0 (.out(X0_out));
  not not_1 (not_1_out, X2_out);
  not not_2 (not_2_out, X1_out);
  not not_3 (not_3_out, X0_out);
  and and_1 (and_1_out, not_1_out, X0_out);
  and and_2 (and_2_out, not_2_out, X0_out);
  and and_3 (and_3_out, X2_out, not_3_out);
  and and_4 (and_4_out, not_1_out, not_3_out);
  not not_4 (not_4_out, X3_out);
  and and_5 (and_5_out, and_1_out, X3_out);
  and and_6 (and_6_out, and_2_out, not_4_out);
  and and_7 (and_7_out, and_3_out, X3_out);
  and and_8 (and_8_out, and_4_out, not_4_out);
  or or_1 (or_1_out, and_5_out, and_6_out);
  or or_2 (or_2_out, and_7_out, and_8_out);
  or or_3 (or_3_out, or_1_out, or_2_out);
  LED led_1 (.in(or_3_out));
endmodule
