// Logisim project CounterMod10.circ as structural Verilog
module JKtrigger (
  input  K,
  input  C,
  input  J,
  input  resetTo_0,
  output Q1,
  output Q2
);

  wire and_1_out, and_2_out, not_1_out, rs_2_out_6, rs_2_out_7, undriven;

  and and_1 (and_1_out, rs_2_out_6, K);
  and and_2 (and_2_out, J, rs_2_out_7);
  RS rs_1 (.S(and_1_out), .C(C), .R(and_2_out), .reset_0(resetTo_0), .reset_1(undriven), .out_6(Q1), .out_7(Q2));
  not not_1 (not_1_out, C);
  RS rs_2 (
    .S(Q2), .C(not_1_out), .R(Q1), .reset_1(resetTo_0), .out_6(rs_2_out_6), .out_7(rs_2_out_7));  // open: reset_0
endmodule

module RS (
  input  S,
  input  C,
  input  R,
  input  reset_0,
  input  reset_1,
  output out_6,
  output out_7
);

  wire and_1_out, and_2_out;

  and and_1 (and_1_out, S, C);
  and and_2 (and_2_out, C, R);
  nor nor_1 (out_6, and_1_out, reset_0, out_7);
  nor nor_2 (out_7, out_6, reset_1, and_2_out);
endmodule

module CounterOnMod_10 (
);

  wire and_1_out, JK0_q2, JK1_q2, JK2_q2, not_1_out, not_2_out, not_3_out, not_4_out, not_5_out, not_6_out,
       not_7_out, not_8_out, or_1_out, Reset_out, x1_1_out;
  wire [3:0] JK0_q1;

  Clock x1_1 (.out(x1_1_out));
  Button Reset (.out(Reset_out));
  or or_1 (or_1_out, Reset_out, not_8_out);
  Hex_Digit_Display counter (.value(JK0_q1));  // open: dp
  JKtrigger JK0 (.K(1'b1), .C(x1_1_out), .J(1'b1), .resetTo_0(or_1_out), .Q1(JK0_q1[0]), .Q2(JK0_q2));
  not not_1 (not_1_out, JK0_q1[0]);
  not not_2 (not_2_out, JK0_q1[2]);
  JKtrigger JK1 (.K(1'b1), .C(JK0_q2), .J(1'b1), .resetTo_0(or_1_out), .Q1(JK0_q1[1]), .Q2(JK1_q2));
  and and_1 (and_1_out, not_1_out, JK0_q1[1], not_2_out, JK0_q1[3]);
  not not_3 (not_3_out, and_1_out);
  not not_4 (not_4_out, not_3_out);
  not not_5 (not_5_out, not_6_out);
  not not_6 (not_6_out, not_4_out);
  not not_7 (not_7_out, not_5_out);
  not not_8 (not_8_out, not_7_out);
  JKtrigger JK2 (.K(1'b1), .C(JK1_q2), .J(1'b1), .resetTo_0(or_1_out), .Q1(JK0_q1[2]), .Q2(JK2_q2));
  JKtrigger JK3 (.K(1'b1), .C(JK2_q2), .J(1'b1), .resetTo_0(or_1_out), .Q1(JK0_q1[3]));  // open: Q2
endmodule
