// Logisim project protipschetchika.circ as structural Verilog: 1 circuit, main circuit main
module main (
);

  wire and_1_out, and_2_out, clock_1_out, j_k_ff_1_qn, j_k_ff_2_qn, j_k_ff_3_qn, nand_1_out, xnor_1_out,
       xnor_2_out, xnor_3_out, xnor_4_out;
  wire [3:0] j_k_ff_1_q;

  Clock clock_1 (.out(clock_1_out));
  Hex_Digit_Display hex_digit_display_1 (.value(j_k_ff_1_q));  // open: dp
  and and_1 (and_1_out, 1'b1, nand_1_out);
  J_K_Flip_Flop j_k_ff_1 (
    .J(and_1_out), .K(1'b1), .clk(clock_1_out), .Q(j_k_ff_1_q[0]), .Qn(j_k_ff_1_qn));  // open: preset, reset
  J_K_Flip_Flop j_k_ff_2 (
    .J(and_1_out), .K(1'b1), .clk(j_k_ff_1_qn), .Q(j_k_ff_1_q[1]), .Qn(j_k_ff_2_qn));  // open: preset, reset
  xnor xnor_1 (xnor_1_out, j_k_ff_1_q[0], 1'b1);
  J_K_Flip_Flop j_k_ff_3 (
    .J(and_1_out), .K(1'b1), .clk(j_k_ff_2_qn), .Q(j_k_ff_1_q[2]), .Qn(j_k_ff_3_qn));  // open: preset, reset
  xnor xnor_2 (xnor_2_out, j_k_ff_1_q[1], 1'b0);
  nand nand_1 (nand_1_out, xnor_1_out, xnor_2_out, xnor_3_out, xnor_4_out);
  and and_2 (and_2_out, j_k_ff_3_qn, nand_1_out);
  xnor xnor_3 (xnor_3_out, j_k_ff_1_q[2], 1'b0);
  J_K_Flip_Flop j_k_ff_4 (.J(and_1_out), .K(1'b1), .clk(and_2_out), .Q(j_k_ff_1_q[3]));  // open: Qn, preset, reset
  xnor xnor_4 (xnor_4_out, j_k_ff_1_q[3], 1'b1);
endmodule
